// Logisim project Obw.circ as structural Verilog: 1 circuit, main circuit main
module main (
  input  not_S,
  input  not_S_2,
  input  T,
  input  not_R,
  input  not_R_2,
  input  S,
  input  not_S_3,
  input  R,
  input  J,
  input  \С ,
  input  S_2,
  input  K,
  input  \С_2 ,
  input  R_2,
  input  not_R_3,
  input  not_S_4,
  input  S_3,
  input  \С_3 ,
  input  R_3,
  input  not_R_4,
  input  D,
  input  \С_4 ,
  input  not_S_5,
  input  not_R_5,
  input  not_S_6,
  input  not_R_6
);

  wire clock_1_out, clock_2_out, nand_1_out, nand_2_out, nand_3_out, nand_4_out, nand_5_out, nand_6_out,
       nand_7_out, nand_8_out, nand_9_out, nand_10_out, nand_11_out, nand_12_out, nand_13_out, nand_14_out,
       nand_15_out, nand_16_out, nand_17_out, nand_18_out, nand_19_out, nand_20_out, nand_21_out,
       nand_22_out, nand_23_out, nand_24_out, nand_25_out, nand_26_out, nand_27_out, nand_28_out,
       nand_29_out, nand_30_out, nand_31_out, nand_32_out, nand_33_out, nand_34_out, nand_35_out,
       nand_36_out, nand_37_out, nand_38_out, nand_39_out, nand_40_out, nand_41_out, nand_42_out,
       nand_43_out, nor_1_out, nor_2_out, nor_3_out, nor_4_out, nor_5_out, nor_6_out, nor_7_out, nor_8_out;

  Clock clock_1 (.out(clock_1_out));
  Clock clock_2 (.out(clock_2_out));
  nand nand_1 (nand_1_out, S_2, \С_2 );
  nand nand_2 (nand_2_out, \С_2 , R_2);
  nand nand_3 (nand_3_out, \С_3 , \С_3 );
  nand nand_4 (nand_4_out, D, D);
  nand nand_5 (nand_5_out, not_S_5, nand_17_out);
  nand nand_6 (nand_6_out, nand_18_out, not_R_5);
  nor nor_1 (nor_1_out, not_S_6, nor_5_out);
  nor nor_2 (nor_2_out, nor_6_out, not_R_6);
  nand nand_7 (nand_7_out, not_S, nand_8_out);
  nand nand_8 (nand_8_out, nand_7_out, not_R);
  nor nor_3 (nor_3_out, S, nor_4_out);
  nor nor_4 (nor_4_out, nor_3_out, R);
  nand nand_9 (nand_9_out, nand_1_out, nand_10_out);
  nand nand_10 (nand_10_out, nand_9_out, nand_2_out);
  nand nand_11 (nand_11_out, S_3, nand_3_out);
  nand nand_12 (nand_12_out, nand_3_out, R_3);
  nand nand_13 (nand_13_out, D, \С_4 );
  nand nand_14 (nand_14_out, nand_13_out, nand_15_out);
  nand nand_15 (nand_15_out, nand_14_out, nand_16_out);
  nand nand_16 (nand_16_out, \С_4 , nand_4_out);
  nand nand_17 (nand_17_out, nand_18_out, nand_5_out, clock_1_out);
  nand nand_18 (nand_18_out, clock_1_out, nand_6_out, nand_17_out);
  nor nor_5 (nor_5_out, nor_6_out, nor_1_out, clock_2_out);
  nor nor_6 (nor_6_out, clock_2_out, nor_2_out, nor_5_out);
  LED led_1 (.in(nand_7_out));
  LED led_2 (.in(nand_8_out));
  LED led_3 (.in(nor_3_out));
  LED led_4 (.in(nor_4_out));
  nand nand_19 (nand_19_out, not_S_4, nand_11_out, nand_20_out);
  nand nand_20 (nand_20_out, nand_19_out, nand_12_out, not_R_4);
  nand nand_21 (nand_21_out, nand_17_out, nand_22_out);
  nand nand_22 (nand_22_out, nand_21_out, nand_18_out);
  nor nor_7 (nor_7_out, nor_5_out, nor_8_out);
  nor nor_8 (nor_8_out, nor_7_out, nor_6_out);
  LED led_5 (.in(nand_9_out));
  LED led_6 (.in(nand_10_out));
  LED led_7 (.in(nand_14_out));
  LED led_8 (.in(nand_15_out));
  LED led_9 (.in(nand_21_out));
  LED led_10 (.in(nand_22_out));
  LED led_11 (.in(nor_7_out));
  LED led_12 (.in(nor_8_out));
  nand nand_23 (nand_23_out, nand_19_out, \С_3 );
  not nand_24 (nand_24_out, nand_20_out);  // NAND_Gate
  nand nand_25 (nand_25_out, not_S_4, nand_23_out, nand_26_out);
  nand nand_26 (nand_26_out, nand_25_out, nand_24_out, not_R_4);
  LED led_13 (.in(nand_25_out));
  LED led_14 (.in(nand_26_out));
  nand nand_27 (nand_27_out, T, T);
  nand nand_28 (nand_28_out, nand_41_out, nand_27_out);
  nand nand_29 (nand_29_out, nand_27_out, nand_40_out);
  nand nand_30 (nand_30_out, nand_43_out, J, \С );
  nand nand_31 (nand_31_out, \С , K, nand_42_out);
  nand nand_32 (nand_32_out, not_S_2, nand_28_out, nand_33_out);
  nand nand_33 (nand_33_out, nand_32_out, nand_29_out, not_R_2);
  nand nand_34 (nand_34_out, not_S_3, nand_30_out, nand_35_out);
  nand nand_35 (nand_35_out, nand_34_out, nand_31_out, not_R_3);
  nand nand_36 (nand_36_out, nand_32_out, T);
  not nand_37 (nand_37_out, nand_33_out);  // NAND_Gate
  nand nand_38 (nand_38_out, nand_34_out, nand_30_out, nand_31_out);
  nand nand_39 (nand_39_out, nand_31_out, nand_30_out, nand_35_out);
  LED led_15 (.in(nand_40_out));
  nand nand_40 (nand_40_out, not_S_2, nand_36_out, nand_41_out);
  LED led_16 (.in(nand_41_out));
  nand nand_41 (nand_41_out, nand_40_out, nand_37_out, not_R_2);
  nand nand_42 (nand_42_out, not_S_3, nand_43_out, nand_38_out);
  nand nand_43 (nand_43_out, nand_39_out, nand_42_out, not_R_3);
  LED led_17 (.in(nand_42_out));
  LED led_18 (.in(nand_43_out));

  // Notes on the sheet:
  //   С
  //   С
  //   1
  //   2
  //   3
  //   4
  //   5
  //   6
  //   7
  //   Q
  //   not Q
  //   Q
  //   not Q
  //   Q
  //   not Q
  //   Q
  //   not Q
  //   Q
  //   not Q
  //   Q
  //   not Q
  //   Q
  //   not Q
  //   8
  //   9
  //   Q
  //   not Q
  //   Q
  //   not Q
endmodule
