// Logisim project D.circ as structural Verilog: 1 circuit, main circuit main
module main (
  output [6:0] out_1,
  output [6:0] out_2
);

  wire clock_2_out, d_ff_1_q, d_ff_2_q, d_ff_3_qn, d_ff_4_qn;

  Clock clock_1 (.out(out_1[5]));
  Clock clock_2 (.out(clock_2_out));
  D_Flip_Flop d_ff_1 (.clk(out_1[5]), .D(d_ff_3_qn), .Q(d_ff_1_q), .en(1'b1));  // open: Qn, preset, reset
  D_Flip_Flop d_ff_2 (.clk(clock_2_out), .D(d_ff_4_qn), .Q(d_ff_2_q), .en(1'b1));  // open: Qn, preset, reset
  D_Flip_Flop d_ff_3 (
    .clk(out_1[5]), .D(d_ff_3_qn), .Q(out_1[6]), .Qn(d_ff_3_qn), .en(d_ff_1_q));  // open: preset, reset
  D_Flip_Flop d_ff_4 (
    .clk(clock_2_out), .D(d_ff_4_qn), .Q(out_2[6]), .Qn(d_ff_4_qn), .en(d_ff_2_q));  // open: preset, reset
  not not_1 (out_1[4], out_1[6]);
  not not_2 (out_2[3], out_2[6]);

  assign out_1[3:0] = {1'b1, {2{out_1[6]}}, 1'b0};
  assign {out_2[5:4], out_2[2:0]} = {2'b01, {2{out_2[6]}}, 1'b0};
endmodule
