// Logisim project JK.circ as structural Verilog: 1 circuit, main circuit main
module main (
  output [5:0] out_1
);

  wire and_1_out, clock_1_out, j_k_ff_2_qn, not_1_out;

  Clock clock_1 (.out(clock_1_out));
  J_K_Flip_Flop j_k_ff_1 (
    .J(not_1_out), .clk(clock_1_out), .K(not_1_out), .Q(out_1[2]), .Qn(out_1[4]), .en(1'b1), .reset(and_1_out));  // open: preset
  not not_1 (not_1_out, clock_1_out);
  xor xor_1 (out_1[3], out_1[4], j_k_ff_2_qn);
  J_K_Flip_Flop j_k_ff_2 (
    .J(out_1[2]), .clk(clock_1_out), .K(out_1[2]), .Q(out_1[5]), .Qn(j_k_ff_2_qn), .en(1'b1),
    .reset(and_1_out));  // open: preset
  and and_1 (and_1_out, out_1[5], out_1[2]);

  assign out_1[1:0] = 2'b01;
endmodule
