// Logisim project T.circ as structural Verilog: 1 circuit, main circuit main
module main (
  output out_1,
  output out_2,
  output out_3,
  output out_4,
  output out_5
);

  wire and_1_out, clock_1_out, decoder_1_out28, decoder_1_out29, decoder_1_out30, not_1_out;
  wire [1:0] t_ff_2_q;

  Clock clock_1 (.out(clock_1_out));
  not not_1 (not_1_out, clock_1_out);
  Decoder #(.select(5), .enable("false")) decoder_1 (
    .out28(decoder_1_out28), .out29(decoder_1_out29), .out30(decoder_1_out30), .sel({3'b111, t_ff_2_q}));  // open: out0, out1, out2, out3, out4, out5, out6, out7, out8, out9, out10, out11, out12, out13, out14, out15, out16, out17, out18, out19, out20, out21, out22, out23, out24, out25, out26, out27, out31
  T_Flip_Flop t_ff_1 (
    .clk(clock_1_out), .T(not_1_out), .Q(t_ff_2_q[1]), .reset(and_1_out), .en(1'b1));  // open: Qn, preset
  T_Flip_Flop t_ff_2 (
    .clk(clock_1_out), .T(t_ff_2_q[1]), .Q(t_ff_2_q[0]), .reset(and_1_out), .en(1'b1));  // open: Qn, preset
  and and_1 (and_1_out, t_ff_2_q[1], t_ff_2_q[0]);
  // Probe on {out_5, out_4, out_3, out_2, out_1}
  Priority_Encoder #(.select(5)) priority_encoder_1 (
    .in2(decoder_1_out28), .in17(decoder_1_out30), .in23(decoder_1_out29),
    .out({out_5, out_4, out_3, out_2, out_1}));  // open: in0, in1, in3, in4, in5, in6, in7, in8, in9, in10, in11, in12, in13, in14, in15, in16, in18, in19, in20, in21, in22, in24, in25, in26, in27, in28, in29, in30, in31, gs, en_out, en_in
endmodule
