// Logisim project cntmv.circ as structural Verilog: 1 circuit, main circuit cntmv
module cntmv (
  input  [11:0] in_1,
  output [11:0] out_2
);

  ROM #(.addrWidth(12), .dataWidth(12)) rom_1 (.addr(in_1), .data(out_2));  // open: sel

  // Notes on the sheet:
  //   contents of rom_1 (hex, n*v repeats v):
  //   187 1c7 a7 c4 1a4 95 84 eb 1d5 1e5 d9 1b9 1b6 1b5 c3 1a3 83 1ca 86 95 94 a4 b3 c8 c5 d4 ed e2 e3 1a8
  //   1d6 1d9 d2 192 1e6 1e9 b2 1b2 1e2 92 1d2 b5 183 1c3 a3 1c8 a8 ca d6 d9 e6 e9 183 c7 e5 196 87 d5 184
  //   195 a4 194 1a7 1a2 1b7 1c4 b6 1c8 b9 1db 1d9 1eb 1ed 1e4 182 1c2 a2 c9 86 c6 98 da ea 1a6 1a9 1d8
  //   1b4 1da 1e3 1e8 93 1d5 b7 1ec 1cb ba 1b8 1e4 1b3 d7 85 94 e7 c5 197 1a5 1d4 b8 cb 1ba 97 e4 b3 a5
  //   1c5 185 d4 194 a6 d8 a9 dc e8 186 ec 198 1c6 e3 b4 1c9 1b7 1d7 d3 193 1da 1e7 1ea c2 1a2 82 1f3 f4
  //   1f5 f6 187 1c7 a7 c4 1a4 95 84 eb 1d5 1e5 de 1b9 1b6 1b5 c3 1a3 83 1ca 86 95 94 a4 b3 c8 c5 d4 ed e2
  //   e3 1a8 1d6 1d9 d2 192 1e6 1e9 b2 1b2 1e2 92 1d2 b5 183 1c3 a3 1c8 a8 ca d6 d9 e6 e9 183 c7 e5 196 87
  //   d5 184 195 a4 194 1a7 1a2 1b7 1c4 b6 1c8 b9 1db 1d9 1eb 1ed 1e4 182 1c2 a2 c9 86 c6 98 da ea 1a6 1a9
  //   1d8 1b4 1da 1e3 1e8 93 1d5 b7 1ec 1cb ba 1b8 1e4 1b3 d7 85 94 e7 c5 197 1a5 1d4 b8 cb 1ba 97 e4 b3
  //   a5 1c5 185 d4 194 a6 d8 a9 dc e8 186 ec 198 1c6 e3 b4 1c9 1b7 1d7 d3 193 1da 1e7 1ea c2 1a2 82 1f3
  //   f4 1f5 f6 187 1c7 a7 c4 1a4 95 84 eb 1d5 1e5 de 1b9 1b6 1b5 c3 1a3 83 1ca 86 95 94 a4 b3 c8 c5 d4 ed
  //   e2 e3 1a8 1d6 1d9 d2 192 1e6 1e9 b2 1b2 1e2 92 1d2 b5 183 1c3 a3 1c8 a8 ca d6 d9 e6 e9 183 c7 e5 196
  //   87 d5 184 195 a4 194 1a7 1a2 1b7 1c4 b6 1c8 b9 1db 1d9 1eb 1ed 1e4 182 1c2 a2 c9 86 c6 98 da ea 1a6
  //   1a9 1d8 1b4 1da 1e3 1e8 93 1d5 b7 1ec 1cb ba 1b8 1e4 1b3 d7 85 94 e7 c5 197 1a5 1d4 b8 cb 1ba 97 e4
  //   b3 a5 1c5 185 d4 194 a6 d8 a9 dc e8 186 ec 198 1c6 e3 b4 1c9 1b7 1d7 d3 193 1da 1e7 1ea c2 1a2 82
  //   1f3 f4 1f5 f6 187 1c7 a7 c4 1a4 95 84 eb 1d5 1e5 de 1b9 1b6 1b5 c3 1a3 83 1ca 86 95 94 a4 b3 c8 c5
  //   d4 ed e2 e3 1a8 1d6 1d9 d2 192 1e6 1e9 b2 1b2 1e2 92 1d2 b5 183 1c3 a3 1c8 a8 ca d6 d9 e6 e9 183 c7
  //   e5 196 87 d5 184 195 a4 194 1a7 1a2 1b7 1c4 b6 1c8 b9 1db 1d9 1eb 1ed 1e4 182 1c2 a2 c9 86 c6 98 da
  //   ea 1a6 1a9 1d8 1b4 1da 1e3 1e8 93 1d5 b7 1ec 1cb ba 1b8 1e4 1b3 d7 85 94 e7 c5 197 1a5 1d4 b8 cb 1ba
  //   97 e4 b3 a5 1c5 185 d4 194 a6 d8 a9 dc e8 186 ec 198 1c6 e3 b4 1c9 1b7 1d7 d3 193 1da 1e7 1ea c2 1a2
  //   82 1f3 f4 1f5 f6 187 1c7 a7 c4 1a4 95 84 eb 1d5 1e5 de 1b9 1b6 1b5 c3 1a3 83 1ca 86 95 94 a4 b3 c8
  //   c5 d4 ed e2 e3 1a8 1d6 1d9 d2 192 1e6 1e9 b2 1b2 1e2 92 1d2 b5 183 1c3 a3 1c8 a8 ca d6 d9 e6 e9 183
  //   c7 e5 196 87 d5 184 195 a4 194 1a7 1a2 1b7 1c4 b6 1c8 b9 1db 1d9 1eb 1ed 1e4 182 1c2 a2 c9 86 c6 98
  //   da ea 1a6 1a9 1d8 1b4 1da 1e3 1e8 93 1d5 b7 1ec 1cb ba 1b8 1e4 1b3 d7 85 94 e7 c5 197 1a5 1d4 b8 cb
  //   1ba 97 e4 b3 a5 1c5 185 d4 194 a6 d8 a9 dc e8 186 ec 198 1c6 e3 b4 1c9 1b7 1d7 d3 193 1da 1e7 1ea c2
  //   1a2 82 1f3 f4 1f5 f6 187 1c7 a7 c4 1a4 95 84 eb 1d5 1e5 de 1b9 1b6 1b5 c3 1a3 83 1ca 86 95 94 a4 b3
  //   c8 c5 d4 ed e2 e3 1a8 1d6 1d9 d2 192 1e6 1e9 b2 1b2 1e2 92 1d2 b5 183 1c3 a3 1c8 a8 ca d6 d9 e6 e9
  //   183 c7 e5 196 87 d5 184 195 a4 194 1a7 1a2 1b7 1c4 b6 1c8 b9 1db 1d9 1eb 1ed 1e4 182 1c2 a2 c9 86 c6
  //   98 da ea 1a6 1a9 1d8 1b4 1da 1e3 1e8 93 1d5 b7 1ec 1cb ba 1b8 1e4 1b3 d7 85 94 e7 c5 197 1a5 1d4 b8
  //   cb 1ba 97 e4 b3 a5 1c5 185 d4 194 a6 d8 a9 dc e8 186 ec 198 1c6 e3 b4 1c9 1b7 1d7 d3 193 1da 1e7 1ea
  //   c2 1a2 82 1f3 f4 1f5 f6 187 1c7 a7 c4 1a4 95 84 eb 1d5 1e5 de 1b9 1b6 1b5 c3 1a3 83 1ca 86 95 94 a4
  //   b3 c8 c5 d4 ed e2 e3 1a8 1d6 1d9 d2 192 1e6 1e9 b2 1b2 1e2 92 1d2 b5 183 1c3 a3 1c8 a8 ca d6 d9 e6
  //   e9 183 c7 e5 196 87 d5 184 195 a4 194 1a7 1a2 1b7 1c4 b6 1c8 b9 1db 1d9 1eb 1ed 1e4 182 1c2 a2 c9 86
  //   c6 98 da ea 1a6 1a9 1d8 1b4 1da 1e3 1e8 93 1d5 b7 1ec 1cb ba 1b8 1e4 1b3 d7 85 94 e7 c5 197 1a5 1d4
  //   b8 cb 1ba 97 e4 b3 a5 1c5 185 d4 194 a6 d8 a9 dc e8 186 ec 198 1c6 e3 b4 1c9 1b7 1d7 d3 193 1da 1e7
  //   1ea c2 1a2 82 1f3 f4 1f5 f6 187 1c7 a7 c4 1a4 95 84 eb 1d5 1e5 de 1b9 1b6 1b5 c3 1a3 83 1ca 86 95 94
  //   a4 b3 c8 c5 d4 ed e2 e3 1a8 1d6 1d9 d2 192 1e6 1e9 b2 1b2 1e2 92 1d2 b5 183 1c3 a3 1c8 a8 ca d6 d9
  //   e6 e9 183 c7 e5 196 87 d5 184 195 a4 194 1a7 1a2 1b7 1c4 b6 1c8 b9 1db 1d9 1eb 1ed 1e4 182 1c2 a2 c9
  //   86 c6 98 da ea 1a6 1a9 1d8 1b4 1da 1e3 1e8 93 1d5 b7 1ec 1cb ba 1b8 1e4 1b3 d7 85 94 e7 c5 197 1a5
  //   1d4 b8 cb 1ba 97 e4 b3 a5 1c5 185 d4 194 a6 d8 a9 dc e8 186 ec 198 1c6 e3 b4 1c9 1b7 1d7 d3 193 1da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
endmodule
