// Logisim project grDeltaMem.circ as structural Verilog: 1 circuit, main circuit grnDeltaMem
module grnDeltaMem (
  input  [6:0] in_1,
  output [23:0] out_2
);

  ROM #(.addrWidth(7), .dataWidth(24)) rom_1 (.addr(in_1), .data(out_2));  // open: sel

  // Notes on the sheet:
  //   contents of rom_1 (hex, n*v repeats v):
  //   28 28028 50028 78028 a0028 c8028 f0028 118028 140028 168028 190028 1b8028 1e0028 208028 230028
  //   258028 280028 2a8028 2d0028 2f8028 320028 348028 370028 398028 3c0028 3e8028 410028 438028 460028
  //   488028 4b0028 4d8028 500028 528028 550028 578028 5a0028 5c8028 5f0028 618028 640028 668028 690028
  //   6b8028 6e0028 708028 730028 758028 780028 7a8028 7d0028 7f8028 820028 848028 870028 898028 8c0028
  //   8e8028 910028 938028 96069b
endmodule
