// Logisim project grnMem2.circ as structural Verilog: 1 circuit, main circuit grnMem2
module grnMem2 (
  input  [6:0] in_1,
  output [31:0] out_2
);

  ROM #(.addrWidth(7), .dataWidth(32)) rom_1 (.addr(in_1), .data(out_2));  // open: sel

  // Notes on the sheet:
  //   contents of rom_1 (hex, n*v repeats v):
  //   204e860 204e861 204e862 204e863 204e864 204e8a0 204e8a1 204e8a2 a04e860 a04e861 a04e862 a04e863
  //   a04e864 a04e865 a04e8a0 a04e8a1 a04e8a2 a04e8e0 a04e8e1 a04e8e2 a04e920 a04e921 a04e922 a04e923
  //   a04e924 a04e960 a04e961 a04e962 a04e9a0 a04e9a1 a04e9a2 a04e9a3 a04e9a4 a04e9a5 a04e9a6 a04e9a7
  //   a04e9a8 a04e9e0 a04e9e1 a04e9e2 a04e9e3 a04e9e4 a04e9e5 a04e9e6 a04e9e7 a04e9e8 c04e860 c04e861
  //   d04e860 d04e861 d04e862 d04e863 d04e864 d04e8a0 d04e8a1 d04e8a2 d04e8a3 d04e8e0 d04e8e1 d04e8e2
  //   700f011
endmodule
