// Logisim project stnMem3.circ as structural Verilog: 1 circuit, main circuit stnMem3
module stnMem3 (
  input  [11:0] in_1,
  output [19:0] out_2
);

  ROM #(.addrWidth(12), .dataWidth(20)) rom_1 (.addr(in_1), .data(out_2));  // open: sel

  // Notes on the sheet:
  //   contents of rom_1 (hex, n*v repeats v):
  //   d004 80480 80382 42005 427c2 42100 d000 42141 8201d 8e200 82111 80000 82410 d302 42100 8230d 40411
  //   56011 82008 8009f d002 9340 40011 82302 e50c 823c3 21b2c 22b2c 23b2c 24b2c 25b2c 26b2c 27b2c 28b2c
  //   29b2c 60b2c 61b2c 62b2c 63b2c 64b2c ca340 42010 82482 42201 80000 d040 82410 8234c 820c2 820d2 80280
  //   8230a 82290 82100 42304 420c0 82111 4234c 42500 80085 8244f 80480 82300 d340 65b2c 66b2c 67b2c 68b2c
  //   69b2c a0b2c a1b2c a2b2c a3b2c a4b2c a5b2c a6b2c a7b2c a8b2c a9b2c e0b2c 1f29d 42045 82010 8e082
  //   8e008 173c5 8e002 42440 82000 82351 80140 42103 40004 823c0 8034d 931e 82000 82302 8d102 17280 82000
  //   ca3c8 8e002 82351 42108 e1b2c e2b2c e3b2c e4b2c e5b2c e6b2c e7b2c e8b2c e9b2c 20b2c 21b2c 22b2c
  //   23b2c 24b2c 25b2c 8278e 4262c 82300 42015 82011 82007 4210c 8e202 d8100 82100 8a09e d002 d000 4eb2c
  //   82080 d100 4200d 42288 82002 82210 82004 d351 8008e 82440 82000 8242c d1302 26b2c 27b2c 28b2c 29b2c
  //   60b2c 61b2c 62b2c 63b2c 64b2c 65b2c 66b2c 67b2c 68b2c cd000 42000 cd742 82003 80000 d401 827d4 82202
  //   82200 423cf d384 dc100 827c2 d00a 82304 cd015 82452 42343 42000 4231e 80008 82004 82002 8276c 8e202
  //   82340 427d1 69b2c a0b2c a1b2c a2b2c a3b2c a4b2c a5b2c a6b2c a7b2c a8b2c a9b2c e0b2c e1b2c 4200e
  //   8228a 8e000 ca011 82000 9002 4008d 82200 d440 d5091 8220d d092 40002 d100 d308 1244a d005 801ca
  //   40080 80342 80010 80100 82440 82102 8d2c4 82210 e2b2c e3b2c e4b2c e5b2c e6b2c e7b2c e8b2c e9b2c
  //   20b2c 21b2c 22b2c 23b2c 24b2c 25b2c 82000 427d1 8250c 8210c 82208 823c5 8e00e d280 102 d5300 80110
  //   c808b 82002 82448 42100 d480 823c0 82311 8210c a02c 8000e 8e0c0 80100 82480 46c d110 82308 26b2c
  //   27b2c 28b2c 29b2c 60b2c 61b2c 62b2c 63b2c 64b2c 65b2c 66b2c 67b2c 68b2c 8244f 8e140 80100 82341
  //   40200 cd000 8230d 42100 8200f 4200f 82540 42000 a004 82487 ce000 82484 823c3 82308 5310f 42111 82345
  //   82300 42100 82502 69b2c 20b2c 21b2c 22b2c 23b2c 24b2c 25b2c 26b2c 27b2c 28b2c 29b2c 60b2c 61b2c
  //   62b2c 63b2c 64b2c 8e104 82001 80108 d44f 82008 80151 8e10e 802cc 82008 80080 80110 cd000 80144 8028e
  //   8201d 900c d311 4245e d140 827c0 d28b d00c 82102 40082 803c0 4200c 82080 4001e d3c5 40002 8e284
  //   65b2c 66b2c 67b2c 68b2c 69b2c a0b2c a1b2c a2b2c a3b2c 82080 8e0c0 42111 d205 82111 17000 82080 82302
  //   8e2c1 d480 42100 82080 4200c 17300 8e151 4200a 82110 42104 4210a 82143 82082 9082 8e280 80780 8200c
  //   420d1 4244c 82001 d5302 8200c 42080 a4b2c a5b2c a6b2c a7b2c a8b2c a9b2c e0b2c e1b2c e2b2c 80280 d340
  //   10014 42300 40011 d102 42002 82300 1f084 8200f 920a 80002 8230f 4000c d004 82091 82282 80308 a102
  //   82000 82300 d010 82083 82480 42340 ca102 82318 82082 82008 90ca 82310 8030c e3b2c e4b2c e5b2c e6b2c
  //   e7b2c e8b2c e9b2c 20b2c 8004a cd000 82310 17202 42342 d012 82304 82140 423d1 82587 8228f 9200 82511
  //   80300 d1100 8234e 823d1 8a111 82451 82451 42104 6b418 d7c0 8028a 80391 42000 42104 8214c 42482 17301
  //   423c8 d5008 80142 21b2c 22b2c 23b2c 24b2c 25b2c 26b2c 27b2c 82340 82104 42005 82088 82004 80083 d7c4
  //   d082 8e440 d11e 8e300 823c0 8e104 8e084 40000 4214a 170cf 823c4 82004 82355 82442 d7c2 82111 42100
  //   8201d 42011 ca2c2 82000 42000 80000 9204 28b2c 29b2c 60b2c 61b2c 62b2c 63b2c 64b2c 65b2c 66b2c 827ac
  //   2b46c 80000 8e140 40143 40142 4e440 c9b2c 43292 8209e 82004 ca32c 4102 8275d 43342 40000 80088 cd42c
  //   d340 80444 ca08c 8e4d1 42200 82345 82348 d284 82002 8200c 8202c 82000 9051 8d300 d011 67b2c 68b2c
  //   69b2c a0b2c a1b2c a2b2c a3b2c 8e00a 82140 8e7c2 82050 40140 8200c 9102 42011 822c2 ce204 42300 d011
  //   8214f 8e280 d08d 82000 d000 4020c 42011 948c 42005 80142 803d1 80200 d144 d7c8 82482 4200d a4b2c
  //   a5b2c a6b2c a7b2c a8b2c a9b2c e0b2c e1b2c e2b2c e3b2c e4b2c e5b2c 52005 cd002 82100 820c4 d10c 82002
  //   8250a 4200c 82351 82010 8038f d208 8200c 82104 42210 8e340 8e011 82751 82005 15440 9780 cd100 82011
  //   82200 d3c0 82000 4078e 827c0 9285 8e080 42305 e6b2c e7b2c e8b2c e9b2c 20b2c 21b2c 22b2c 23b2c 24b2c
  //   82008 82000 82004 c0000 9000 cd302 82140 8e304 d308 8e151 42308 82311 42200 82402 82344 82007 8e100
  //   d10d 9200 a311 8e44f 803c5 db42c 82102 42080 8200d dc304 8244e cd751 42091 82000 42100 25b2c 26b2c
  //   27b2c 28b2c 29b2c 60b2c 61b2c 62b2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
endmodule
